# Fritzing sketch esp32 interfaced with dht 11 sensor (saved by Fritzing 0.9.3b)
breadboards: 1

parts:
  DHT1 = Humidity and Temperature Sensor DHT11
  MH-ET_LIVE_ESP32_DEVKIT1 = MH-ET LIVE ESP32 DEVKIT 38 pins

nets:
  VCC: DHT1.Vcc, MH-ET_LIVE_ESP32_DEVKIT1.5V
  N1: DHT1.Data-signal, MH-ET_LIVE_ESP32_DEVKIT1.IO27
  N2: DHT1.GND_1, MH-ET_LIVE_ESP32_DEVKIT1.CMD

custom parts:
  Humidity and Temperature Sensor DHT11: Digital relative humidity & temperature sensor DHT11
  MH-ET LIVE ESP32 DEVKIT 38 pins: http://mh.nodebb.com/topic/2/mh-et-live-esp32-devkit
