# Fritzing sketch esp32 with temperature sensor (saved by Fritzing 0.9.3b)
breadboards: 1

parts:
  U1 = TMP36 [package=to-92]
  MH-ET_LIVE_ESP32_DEVKIT1 = MH-ET LIVE ESP32 DEVKIT 38 pins

nets:
  VCC: U1.VCC, MH-ET_LIVE_ESP32_DEVKIT1.5V
  N1: U1.VOUT, MH-ET_LIVE_ESP32_DEVKIT1.IO2
  GND: U1.GND, MH-ET_LIVE_ESP32_DEVKIT1.GND

custom parts:
  MH-ET LIVE ESP32 DEVKIT 38 pins: http://mh.nodebb.com/topic/2/mh-et-live-esp32-devkit
