# Fritzing sketch raspberry pi pico interfaced with dht 11 sensor (saved by Fritzing 0.9.3b)
breadboards: 1

parts:
  Mod1 = Raspberry Pi Pico
  DHT1 = Humidity and Temperature Sensor DHT11

nets:
  N1: Mod1.pin_3, Mod1.pin_28, Mod1.pin_42, DHT1.GND_1
  N2: Mod1.pin_34, DHT1.Data-signal
  N3: Mod1.pin_36, DHT1.Vcc

custom parts:
  Raspberry Pi Pico: Raspberry Pi Pico. Based around the RP2040 microcontroller the Pico is a low cost microcontroller device bringing Raspberry Pi quality, cost, and easy of use to the microcontroller space. Jan 2021, Split part in to two versions: tht (this one) and SMD. This one will drill holes for a .1 in header in pcb to allow plugging in the module as well as providing pads to solder the module to the top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
  Humidity and Temperature Sensor DHT11: Digital relative humidity & temperature sensor DHT11
